# Fritzing sketch vocoder_raspberry_pi (saved by Fritzing 0.9.3b)
breadboards: 1

parts:
  ADC1 = MCP3008 [package=dil16]
  Part2 = Adafruit Pi Cobbler Plus [part_number="Adafruit #2029"]
  R1 = Rotary Potentiometer (Small) [maximum_resistance=100kΩ package=THT]

nets:
  N1: ADC1.CH0, R1.wiper
  N2: ADC1.DGND, R1.leg1
  N3: ADC1.CS/SHDN, Part2.GPIO25
  N4: ADC1.Din, Part2.GPIO24
  N5: ADC1.Dout, Part2.GPIO23
  N6: ADC1.CLK, Part2.GPIO18
  N7: ADC1.AGND, Part2.GND
  N8: ADC1.VREF, ADC1.VDD

custom parts:
  Adafruit Pi Cobbler Plus: The Raspberry Pi B+/Pi 2/ Pi 3 has landed on the Maker World like a 40-GPIO pinned, quad-USB ported, credit card sized bomb of DIY joy. And while you can use most of our great Model B accessories by hooking up our downgrade cable, its probably a good time to upgrade your set up and accessorize using all of the Model B+'s / Pi 2's / Pi 3's 40 pins. That's why we now carry the Adafruit Assembled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
